// Logisim project Circuits.circ as structural Verilog: 4 circuits, main circuit RFile
module SCP (
  input  PCclear
);

  wire CLK_out, comparator_1_eq, comparator_1_gt, comparator_1_lt, comparator_2_eq, comparator_2_gt,
       comparator_2_lt, ExtOp, MemR, MemW, multiplexer_5_out, not_1_out, or_1_out, or_2_out, RegWrite;
  wire [1:0] f, in2Sel, PCcs, RegDst, ShiftImmReg, WData;
  wire [2:0] BROP, Imm3, Imm5, multiplexer_1_out;
  wire [3:0] AlUOP;
  wire [4:0] Op;
  wire [5:3] Imm11;
  wire [15:0] adder_2_out, adder_3_out, adder_4_out, alu_1_aluoutput, Buss1, Buss2, DtatO, imm2U_imm3L,
       imm2U_imm3Ls, Imm3e, imm11s, imm11Z, multiplexer_2_out, multiplexer_3_out, multiplexer_4_out, PC,
       PC_1, PCoption, ram_1_data, sExtend5, ZExtend5;

  Register #(.width(16)) u_PC (.D(PCoption), .en(1'b1), .Q(PC), .clk(CLK_out), .clr(PCclear));
  Clock CLK (.out(CLK_out));
  Adder #(.width(16)) adder_1 (.a(PC), .b(16'h1), .out(PC_1), .cin(1'b0));  // open: cout
  ROM #(.addrWidth(16), .dataWidth(16)) rom_1 (.addr(PC), .data({f, Imm5, Imm11, Imm3, Op}));  // open: sel
  assign ZExtend5 = {{11{1'b0}}, {f, Imm5}};  // Bit_Extender bit_extender_1
  assign sExtend5 = {{11{f[1]}}, {f, Imm5}};  // Bit_Extender bit_extender_2
  assign imm2U_imm3Ls = {{11{f[1]}}, {f, Imm3}};  // Bit_Extender bit_extender_3
  assign imm2U_imm3L = {{11{1'b0}}, {f, Imm3}};  // Bit_Extender bit_extender_4
  assign imm11s = {{5{f[1]}}, {f, Imm5, Imm11, Imm3}};  // Bit_Extender bit_extender_5
  assign imm11Z = {{5{1'b0}}, {f, Imm5, Imm11, Imm3}};  // Bit_Extender bit_extender_6
  assign Imm3e = {{13{1'b0}}, Imm3};  // Bit_Extender bit_extender_7
  Multiplexer #(.select(2), .width(3), .enable("false")) multiplexer_1 (
    .in0(Imm3), .in1(3'b111), .in2(3'b001), .out(multiplexer_1_out), .sel(RegDst));  // open: in3
  controlsignal controlsignal_1 (
    .OPCODE(Op), .f(f), .RegDst(RegDst), .RegWrite(RegWrite), .ExtOp(ExtOp), .in2Sel(in2Sel), .MemW(MemW),
    .MemR(MemR), .WData(WData), .ALUop(AlUOP), .ShiftImmReg(ShiftImmReg), .BROP(BROP), .PCcs(PCcs));
  RFile rfile_1 (
    .Rs1(Imm11), .Rs2(Imm5), .Busd(DtatO), .Rd(multiplexer_1_out), .RegWrite(RegWrite), .Buss1(Buss1),
    .Buss2(Buss2), .CLK(CLK_out));
  Multiplexer #(.width(16), .enable("false")) multiplexer_2 (
    .in0(ZExtend5), .in1(sExtend5), .out(multiplexer_2_out), .sel(ExtOp));
  Multiplexer #(.select(2), .width(16), .enable("false")) multiplexer_3 (
    .in0(Buss2), .in1(multiplexer_2_out), .in2(imm2U_imm3L), .in3(imm11Z), .out(multiplexer_3_out),
    .sel(in2Sel));
  Comparator #(.width(16)) comparator_1 (
    .a(Buss1), .b(Buss2), .gt(comparator_1_gt), .eq(comparator_1_eq), .lt(comparator_1_lt));
  Comparator #(.width(16), .mode("unsigned")) comparator_2 (
    .a(Buss1), .b(Buss2), .gt(comparator_2_gt), .eq(comparator_2_eq), .lt(comparator_2_lt));
  ALU alu_1 (
    .input1(Buss1), .input2(multiplexer_3_out), .ALUoutput(alu_1_aluoutput), .ALUop(AlUOP),
    .ShiftImmReg(ShiftImmReg));
  Adder #(.width(16)) adder_2 (.a(imm2U_imm3Ls), .b(PC), .out(adder_2_out), .cin(1'b0));  // open: cout
  not not_1 (not_1_out, comparator_1_eq);
  Multiplexer #(.width(16), .enable("false")) multiplexer_4 (
    .in0(PC_1), .in1(adder_2_out), .out(multiplexer_4_out), .sel(multiplexer_5_out));
  Multiplexer #(.select(3), .enable("false")) multiplexer_5 (
    .in0(comparator_1_eq), .in1(not_1_out), .in2(comparator_1_lt), .in3(or_1_out), .in4(comparator_2_lt),
    .in5(or_2_out), .out(multiplexer_5_out), .sel(BROP));  // open: in6, in7
  or or_1 (or_1_out, comparator_1_gt, comparator_1_eq);
  or or_2 (or_2_out, comparator_2_gt, comparator_2_eq);
  RAM #(.addrWidth(16), .dataWidth(16), .bus("separate")) ram_1 (
    .addr(alu_1_aluoutput), .din(Buss2), .data(ram_1_data), .str(MemW), .clk(CLK_out), .ld(MemR));  // open: sel, clr
  Adder #(.width(16)) adder_3 (.a(imm11s), .b(PC), .out(adder_3_out), .cin(1'b0));  // open: cout
  Adder #(.width(16)) adder_4 (.a(sExtend5), .b(Buss1), .out(adder_4_out), .cin(1'b0));  // open: cout
  Multiplexer #(.select(2), .width(16), .enable("false")) multiplexer_6 (
    .in0(alu_1_aluoutput), .in1(ram_1_data), .in2(PC_1), .out(DtatO), .sel(WData));  // open: in3
  Multiplexer #(.select(2), .width(16), .enable("false")) multiplexer_7 (
    .in0(PC_1), .in1(multiplexer_4_out), .in2(adder_3_out), .in3(adder_4_out), .out(PCoption), .sel(PCcs));

  // Other names for the same wires on the sheet: Imm11 (some bits) = {f, Imm5, Imm3}; rd[2:0] = Imm3;
  //   rs1[2:0] = Imm11; rs2[2:0] = Imm5; Imm2[1:0] = f; Imm5[4:3] = f

  // Notes on the sheet:
  //   contents of rom_1 (hex, n*v repeats v):
  //   14c 96c 1380 53a0 93e0 1381 53a1 93a1 13a2 53a2 93a2 d3a2 1283 12a4 12e5 1286 12a7 12e8 4a89 4aaa
  //   4aeb 1f0d 938e 534f 9*0 5350 9*0 5351 5352 9*0 9373 a994 35 56 0 108c 14d7 3470 2cc8 55 2683 3470
  //   2cc8 55 2683 202c 31ad 15
endmodule

module RFile (
  input  [2:0] Rs1,
  input  [2:0] Rs2,
  input  [15:0] Busd,
  input  [2:0] Rd,
  input  RegWrite,
  input  CLK,
  output [15:0] Buss1,
  output [15:0] Buss2
);

  wire and_1_out, and_2_out, and_3_out, and_4_out, and_5_out, and_6_out, and_7_out, decoder_1_out0,
       decoder_2_out0, decoder_2_out1, decoder_2_out2, decoder_2_out3, decoder_2_out4, decoder_2_out5,
       decoder_2_out6, decoder_2_out7, decoder_3_out0, decoder_3_out1, decoder_3_out2, decoder_3_out3,
       decoder_3_out4, decoder_3_out5, decoder_3_out6, decoder_3_out7, R1, R2, R3, R4, R5, R6, R7;
  wire [15:0] R1_q, R2_q, R3_q, R4_q, R5_q, R6_q, R7_q;

  Decoder #(.select(3), .enable("false")) decoder_1 (
    .out0(decoder_1_out0), .out1(R1), .out2(R2), .out3(R3), .out4(R4), .out5(R5), .out6(R6), .out7(R7),
    .sel(Rd));
  and and_1 (and_1_out, R1, RegWrite);
  and and_2 (and_2_out, R2, RegWrite);
  and and_3 (and_3_out, R3, RegWrite);
  and and_4 (and_4_out, R4, RegWrite);
  and and_5 (and_5_out, R5, RegWrite);
  and and_6 (and_6_out, R6, RegWrite);
  and and_7 (and_7_out, R7, RegWrite);
  Register #(.width(16)) u_R1 (.D(Busd), .en(and_1_out), .Q(R1_q), .clk(CLK));  // open: clr
  assign Buss1 = decoder_2_out1 ? R1_q : 16'bz;  // Controlled_Buffer controlled_buffer_1
  Register #(.width(16)) u_R2 (.D(Busd), .en(and_2_out), .Q(R2_q), .clk(CLK));  // open: clr
  assign Buss1 = decoder_2_out2 ? R2_q : 16'bz;  // Controlled_Buffer controlled_buffer_2
  Register #(.width(16)) u_R3 (.D(Busd), .en(and_3_out), .Q(R3_q), .clk(CLK));  // open: clr
  assign Buss1 = decoder_2_out3 ? R3_q : 16'bz;  // Controlled_Buffer controlled_buffer_3
  Register #(.width(16)) u_R4 (.D(Busd), .en(and_4_out), .Q(R4_q), .clk(CLK));  // open: clr
  assign Buss1 = decoder_2_out4 ? R4_q : 16'bz;  // Controlled_Buffer controlled_buffer_4
  assign Buss1 = decoder_2_out5 ? R5_q : 16'bz;  // Controlled_Buffer controlled_buffer_5
  Register #(.width(16)) u_R5 (.D(Busd), .en(and_5_out), .Q(R5_q), .clk(CLK));  // open: clr
  Register #(.width(16)) u_R6 (.D(Busd), .en(and_6_out), .Q(R6_q), .clk(CLK));  // open: clr
  assign Buss1 = decoder_2_out6 ? R6_q : 16'bz;  // Controlled_Buffer controlled_buffer_6
  assign Buss1 = decoder_2_out7 ? R7_q : 16'bz;  // Controlled_Buffer controlled_buffer_7
  Register #(.width(16)) u_R7 (.D(Busd), .en(and_7_out), .Q(R7_q), .clk(CLK));  // open: clr
  assign Buss1 = decoder_2_out0 ? {16{1'b0}} : 16'bz;  // Controlled_Buffer controlled_buffer_8
  Decoder #(.select(3), .enable("false")) decoder_2 (
    .out0(decoder_2_out0), .out1(decoder_2_out1), .out2(decoder_2_out2), .out3(decoder_2_out3),
    .out4(decoder_2_out4), .out5(decoder_2_out5), .out6(decoder_2_out6), .out7(decoder_2_out7), .sel(Rs1));
  assign Buss2 = decoder_3_out1 ? R1_q : 16'bz;  // Controlled_Buffer controlled_buffer_9
  assign Buss2 = decoder_3_out2 ? R2_q : 16'bz;  // Controlled_Buffer controlled_buffer_10
  assign Buss2 = decoder_3_out3 ? R3_q : 16'bz;  // Controlled_Buffer controlled_buffer_11
  assign Buss2 = decoder_3_out4 ? R4_q : 16'bz;  // Controlled_Buffer controlled_buffer_12
  assign Buss2 = decoder_3_out5 ? R5_q : 16'bz;  // Controlled_Buffer controlled_buffer_13
  assign Buss2 = decoder_3_out6 ? R6_q : 16'bz;  // Controlled_Buffer controlled_buffer_14
  assign Buss2 = decoder_3_out7 ? R7_q : 16'bz;  // Controlled_Buffer controlled_buffer_15
  Decoder #(.select(3), .enable("false")) decoder_3 (
    .out0(decoder_3_out0), .out1(decoder_3_out1), .out2(decoder_3_out2), .out3(decoder_3_out3),
    .out4(decoder_3_out4), .out5(decoder_3_out5), .out6(decoder_3_out6), .out7(decoder_3_out7), .sel(Rs2));
  assign Buss2 = decoder_3_out0 ? {16{1'b0}} : 16'bz;  // Controlled_Buffer controlled_buffer_16
endmodule

module ALU (
  input  [15:0] input1,
  input  [15:0] input2,
  input  [3:0] ALUop,
  input  [1:0] ShiftImmReg,
  output [15:0] ALUoutput
);

  wire comparator_1_lt, comparator_2_lt;
  wire [3:0] bit_extender_1_out, bit_extender_2_out, bit_extender_3_out, multiplexer_1_out;
  wire [15:0] adder_1_out, and_1_out, bit_extender_4_out, bit_extender_5_out, bit_extender_6_out, or_1_out,
       shifter_1_out, shifter_2_out, shifter_3_out, shifter_4_out, subtractor_1_out, xor_1_out;

  assign bit_extender_1_out = {{1{1'b0}}, input2[2:0]};  // Bit_Extender bit_extender_1
  assign bit_extender_2_out = {{2{1'b0}}, input2[1:0]};  // Bit_Extender bit_extender_2
  assign bit_extender_3_out = {{3{1'b0}}, input2[0]};  // Bit_Extender bit_extender_3
  Multiplexer #(.select(2), .width(4), .enable("false")) multiplexer_1 (
    .in0(input2[3:0]), .in1(bit_extender_1_out), .in2(bit_extender_2_out), .in3(bit_extender_3_out),
    .out(multiplexer_1_out), .sel(ShiftImmReg));
  assign bit_extender_4_out = {{5{1'b0}}, input2[15:5]};  // Bit_Extender bit_extender_4
  assign xor_1_out = input1 ^ input2;  // XOR_Gate xor_1, 16 bits wide
  assign or_1_out = input1 | input2;  // OR_Gate or_1, 16 bits wide
  assign and_1_out = input1 & input2;  // AND_Gate and_1, 16 bits wide
  Adder #(.width(16)) adder_1 (.a(input1), .b(input2), .out(adder_1_out));  // open: cin, cout
  Subtractor #(.width(16)) subtractor_1 (.a(input1), .b(input2), .out(subtractor_1_out));  // open: bin, bout
  Comparator #(.width(16)) comparator_1 (.a(input1), .b(input2), .lt(comparator_1_lt));  // open: gt, eq
  Comparator #(.width(16), .mode("unsigned")) comparator_2 (
    .a(input1), .b(input2), .lt(comparator_2_lt));  // open: gt, eq
  Shifter #(.width(16)) shifter_1 (.in(input1), .\dist (multiplexer_1_out), .out(shifter_1_out));
  Shifter #(.width(16), .shift("lr")) shifter_2 (.in(input1), .\dist (multiplexer_1_out), .out(shifter_2_out));
  Shifter #(.width(16), .shift("ar")) shifter_3 (.in(input1), .\dist (multiplexer_1_out), .out(shifter_3_out));
  Shifter #(.width(16)) shifter_4 (.in(bit_extender_4_out), .\dist (4'b0101), .out(shifter_4_out));
  assign bit_extender_5_out = {{15{1'b0}}, comparator_1_lt};  // Bit_Extender bit_extender_5
  assign bit_extender_6_out = {{15{1'b0}}, comparator_2_lt};  // Bit_Extender bit_extender_6
  Multiplexer #(.select(4), .width(16), .enable("false")) multiplexer_2 (
    .in0(xor_1_out), .in1(or_1_out), .in2(and_1_out), .in3(adder_1_out), .in4(subtractor_1_out),
    .in5(bit_extender_5_out), .in6(bit_extender_6_out), .in7(shifter_1_out), .in8(shifter_2_out),
    .in9(shifter_3_out), .in10(shifter_4_out), .out(ALUoutput), .sel(ALUop));  // open: in11, in12, in13, in14, in15
endmodule

module controlsignal (
  input  [4:0] OPCODE,
  input  [1:0] f,
  output [1:0] RegDst,
  output RegWrite,
  output ExtOp,
  output [1:0] in2Sel,
  output MemW,
  output MemR,
  output [1:0] WData,
  output [3:0] ALUop,
  output [1:0] ShiftImmReg,
  output [2:0] BROP,
  output [1:0] PCcs
);

  ROM #(.addrWidth(5), .dataWidth(10)) rom_1 (
    .addr(OPCODE), .data({RegDst, RegWrite, ExtOp, in2Sel, MemW, MemR, WData}));  // open: sel
  ROM #(.addrWidth(7), .dataWidth(6)) rom_2 (.addr({f, OPCODE}), .data({ShiftImmReg, ALUop}));  // open: sel
  ROM #(.addrWidth(5), .dataWidth(5)) rom_3 (.addr(OPCODE), .data({BROP, PCcs}));  // open: sel

  // Notes on the sheet:
  //   contents of rom_1 (hex, n*v repeats v):
  //   c0 c0 c0 9*d0 95 29 6*21 2b0 0 182 82
  //   contents of rom_2 (hex, n*v repeats v):
  //   0 7 3 3 5 6 0 1 2 7 8 9 3 3 4 4 5 5 6 6 a 11*0 1 8 4 3 5 6 0 1 2 7 8 9 3 3 4 4 5 5 6 6 a 11*0 2 9 5
  //   3 5 6 0 1 2 7 8 9 3 3 4 4 5 5 6 6 a 13*0 6 3 5 6 0 1 2 7 8 9 3 3 4 4 5 5 6 6 a
  //   contents of rom_3 (hex, n*v repeats v):
  //   14*0 1 5 9 d 11 15 0 2 2 3
endmodule
